// Logisim project 24a.circ as structural Verilog: 1 circuit, main circuit main
module main (
);

  wire bfw_frj_out, bqk_out, djm_out, ffh_out, fgs_out, fst_vdt_out, gnj_out, hwm_out, kjc_out, kpj_out,
       kwq_out, mjb_out, nrd_out, ntg_out, pbm_out, psh_out, qhw_out, rvg_out, tgd_out, tnw_out, wpb_out;
  wire [12:0] z0_out;

  and rvg (rvg_out, kjc_out, fst_vdt_out);
  and z10 (z0_out[10], bfw_frj_out, bfw_frj_out);
  or fst_vdt (fst_vdt_out, 1'b1, 1'b1);
  or bfw_frj (bfw_frj_out, tnw_out, fst_vdt_out);
  and hwm (hwm_out, fst_vdt_out, nrd_out);
  xor z0 (z0_out[0], bfw_frj_out, mjb_out);
  and z3 (z0_out[3], hwm_out, bqk_out);
  xor ntg (ntg_out, 1'b1, 1'b1);
  xor mjb (mjb_out, ntg_out, fgs_out);
  xor z4 (z0_out[4], bfw_frj_out, qhw_out);
  // Probe on {z0_out[12:8], z0_out[8], z0_out[6:2], z0_out[12], z0_out[0]}
  or tnw (tnw_out, 1'b0, 1'b1);
  and pbm (pbm_out, 1'b1, 1'b1);
  or gnj (gnj_out, tnw_out, pbm_out);
  and z2 (z0_out[2], gnj_out, gnj_out, wpb_out);
  and z11 (z0_out[11], gnj_out, tgd_out);
  or nrd (nrd_out, 1'b0, 1'b1);
  or qhw (qhw_out, pbm_out, djm_out);
  or kpj (kpj_out, pbm_out, djm_out);
  and djm (djm_out, 1'b1, 1'b1);
  or bqk (bqk_out, nrd_out, ffh_out);
  xor wpb (wpb_out, nrd_out, fgs_out);
  or z6 (z0_out[6], bfw_frj_out, bqk_out);
  or z7_z8 (z0_out[8], bqk_out, bfw_frj_out);
  or psh (psh_out, 1'b1, 1'b1);
  xor z1_z12 (z0_out[12], rvg_out, tgd_out);
  xor z9 (z0_out[9], qhw_out, tgd_out);
  and kjc (kjc_out, 1'b0, 1'b1);
  xor ffh (ffh_out, 1'b1, 1'b1);
  xor tgd (tgd_out, psh_out, fgs_out);
  or z5 (z0_out[5], kpj_out, kwq_out);
  or fgs (fgs_out, 1'b1, 1'b1);
  or kwq (kwq_out, ntg_out, kjc_out);

  // Notes on the sheet:
  //   x0
  //   y0
  //   x1
  //   y1
  //   x2
  //   y2
  //   x3
  //   y3
  //   x4
  //   y4
endmodule
